# Fritzing sketch lidar-pcb1 (saved by Fritzing 0.9.3b)
circuit board: 5cm x 5cm
breadboards: 1

parts:
  J1 = screw terminal, 6 pins
  Part1 = Arduino Nano (Rev3.0) (ICSP)
  Pololu_A1 = Pololu A4988 [package=SO16]

nets (from the pcb view):
  GND: J1.pin1, Part1.GND, Pololu_A1.GND
  5V: J1.pin2, Part1.5V, Pololu_A1.VDD
  N1: J1.pin3, J1.pin4
  N2: J1.pin5, Part1.A5
  N3: J1.pin6, Part1.A4
  N4: Part1.D2, Pololu_A1.DIR
  N5: Part1.D3, Pololu_A1.STEP
  N6: Part1.D4, Pololu_A1.ENABLE
  N7: Pololu_A1.RESET, Pololu_A1.SLEEP
